# Fritzing sketch TB08.1_cricuit (saved by Fritzing 0.9.0b)
circuit board: 6.99908cm x 5.41866cm
breadboards: 1

parts:
  INA125P1 = INA125P [package="DIP16 [THT]"]
  R1 = Resistor [tolerance=±5% resistance=220 package=THT]
  J3 = shrouded pin header, 20 pins [form="♂ (shrouded male)"]
  J4 = female pin header, 2 pins [form="♀ (female)"]
  part = shrouded pin header, 20 pins [form="♂ (shrouded male)"]  # not connected
  Bauteil1 = Arduino Uno (Rev3)

nets:
  N1: INA125P1.V+, INA125P1.SLEEP, J3.pin2, Bauteil1.5V
  N2: INA125P1.V-, INA125P1.IA_Ref, INA125P1.V_Ref_BG, J3.pin16, J3.pin19, Bauteil1.GND
  N3: INA125P1.V_Ref_OUT, INA125P1.V_0, Bauteil1.AREF
  N4: INA125P1.V_In_+, J3.pin20
  N5: INA125P1.V_In_-, J3.pin1
  N6: INA125P1.R_G#7, R1.Pin_1
  N7: INA125P1.V_Ref_10, R1.Pin_0
  N8: INA125P1.V_Ref_5, INA125P1.V_Ref_2.5, Bauteil1.A0
  N9: J3.pin3, J4.pin1
  N10: J3.pin4, J4.pin2
  N11: J3.pin11, Bauteil1.D13/SCK
  N12: J3.pin12, Bauteil1.D11_PWM/MOSI
  N13: J3.pin13, Bauteil1.D12/MISO
  N14: J3.pin14, Bauteil1.D10_PWM/SS
  N15: J3.pin15, Bauteil1.3V3

custom parts:
  INA125P: The INA125 is a low power, high accuracy instrumen- tation amplifier with a precision voltage reference. It provides complete bridge excitation and precision dif- ferential-input amplification on a single integrated circuit
