# Fritzing sketch TB08_cricuit (saved by Fritzing 0.8.3b)
circuit board: 6.99908cm x 5.41866cm
breadboards: 1

parts:
  Bauteil1 = Arduino Uno (Rev3)
  INA125P1 = INA125P [package="DIP16 [THT]"]
  R1 = Resistor [tolerance=±5% resistance=220 package=THT]
  J3 = shrouded pin header, 20 pins [form="♂ (shrouded male)"]
  J4 = female pin header, 2 pins [form="♀ (female)"]

nets:
  N1: Bauteil1.A0, INA125P1.V_Ref_5, INA125P1.V_Ref_2.5
  N2: Bauteil1.ICSP_SCK, Bauteil1.D13/SCK, J3.pin10
  N3: Bauteil1.GND, INA125P1.V-, INA125P1.IA_Ref, INA125P1.V_Ref_BG, J3.pin2, J3.pin5
  N4: Bauteil1.D10_PWM/SS, J3.pin7
  N5: Bauteil1.D11_PWM/MOSI, J3.pin9
  N6: Bauteil1.D12/MISO, J3.pin8
  N7: Bauteil1.3V3, J3.pin6
  N8: Bauteil1.5V, INA125P1.V+, INA125P1.SLEEP, J3.pin19
  N9: INA125P1.V_Ref_OUT, INA125P1.V_0
  N10: INA125P1.V_In_+, J3.pin1
  N11: INA125P1.V_In_-, J3.pin20
  N12: INA125P1.R_G#7, R1.Pin_1
  N13: INA125P1.V_Ref_10, R1.Pin_0
  N14: J3.pin3, J4.pin1
  N15: J3.pin4, J4.pin2

custom parts:
  INA125P: The INA125 is a low power, high accuracy instrumen- tation amplifier with a precision voltage reference. It provides complete bridge excitation and precision dif- ferential-input amplification on a single integrated circuit
